# Fritzing sketch Sketch (saved by Fritzing 0.9.3b)
breadboards: 1

parts:
  Part1 = Arduino Uno (Rev3)  # not connected
  R1 = Resistor [tolerance=±5% resistance=100 package="2512 [SMD]"]
  LED1 = LED - 3mm [color="Red (633nm)" package="3 mm [THT]"]
  R2 = Resistor [tolerance=±5% resistance=100 package="2512 [SMD]"]  # not connected
  LED2 = LED - 3mm [color="Yellow (595nm)" package="3 mm [THT]"]  # not connected
  R3 = Resistor [tolerance=±5% resistance=100 package="2512 [SMD]"]  # not connected
  LED3 = LED - 3mm [color="Yellow (595nm)" package="3 mm [THT]"]  # not connected

nets:
  N1: R1.Pin_1, LED1.anode
