# Fritzing sketch Sketch 2 (saved by Fritzing 0.9.3b)
breadboards: 1

parts:
  Part1 = Arduino Uno (Rev3)
  K1 = Relay [part_number=FRS1B-S package=THT]
  R1 = Resistor [tolerance=±5% resistance=100 package="0805 [SMD]"]
  LED1 = smd LED [color="Red (633nm)" package="1206 [SMD]"]
  VCC1 = Battery block 9V

nets:
  N1: Part1.D13/SCK, K1.A
  N2: Part1.GND, K1.B
  N3: K1.COIL2, VCC1.-
  N4: R1.Pin_1, LED1.cathode
  N5: LED1.anode, VCC1.+
