# Fritzing sketch Sketch (saved by Fritzing 0.9.3b)
breadboards: 1

parts:
  Q1 = NPN-Transistor [part_number=BC547 package="TO92 [THT]"]
  VCC1 = Battery block 9V
  R1 = Resistor [tolerance=±5% resistance=10k package="0603 [SMD]"]
  R2 = Resistor [tolerance=±5% resistance=100 package="0603 [SMD]"]
  LED1 = smd LED [color="Red (633nm)" package="0603 [SMD]"]
  Part1 = Arduino Uno (Rev3)

nets:
  N1: Q1.E, VCC1.+
  N2: Q1.B, R1.Pin_1
  N3: Q1.C, R2.Pin_0
  N4: VCC1.-, LED1.cathode, Part1.GND
  N5: R1.Pin_0, Part1.D6_PWM
  N6: R2.Pin_1, LED1.anode
